# Fritzing sketch strix-takeover-breadboard (saved by Fritzing 1.0.6)
breadboards: 1

parts:
  Nano1 = Arduino Nano (Rev3.0)
  R1 = Resistor [resistance=4.7k tolerance=±5% package=THT]
  C1 = Ceramic Capacitor [capacitance=1µF package="100 mil [THT, multilayer]"]
  R2 = Resistor [resistance=4.7k tolerance=±5% package=THT]
  C2 = Ceramic Capacitor [capacitance=1µF package="100 mil [THT, multilayer]"]
  SR04_frontLeft = HC-SR04 Ultrasonic Distance Sensor
  SR04_frontRight = HC-SR04 Ultrasonic Distance Sensor
  LevelShifter1 = I2C level shifter bidirectional
  ToF_VL53L4CD = Header 4 [package=jst-4-pth]
  TriggerPotConnector = Header 3 [package=molex-1x3_lock]
  WheelPotConnector = Header 3 [package=molex-1x3_lock]

nets:
  GND: Nano1.GND, C1.1, C2.1, SR04_frontLeft.GND, SR04_frontRight.GND, LevelShifter1.GND, ToF_VL53L4CD.4, TriggerPotConnector.3, WheelPotConnector.3
  N1: Nano1.D2, SR04_frontLeft.TRIG
  N2: Nano1.D3, SR04_frontLeft.ECHO
  N3: Nano1.D4, SR04_frontRight.TRIG
  N4: Nano1.D5, SR04_frontRight.ECHO
  N5: Nano1.D9, R1.Pin_0
  N6: Nano1.D10, R2.Pin_0
  VCC: Nano1.5V, SR04_frontLeft.VCC, SR04_frontRight.VCC, LevelShifter1.HV
  N7: Nano1.A5, LevelShifter1.HV2
  N8: Nano1.A4, LevelShifter1.HV1
  N9: Nano1.A0, TriggerPotConnector.1, WheelPotConnector.1
  N10: Nano1.3V3, LevelShifter1.LV, ToF_VL53L4CD.3
  N11: R1.Pin_1, C1.0, TriggerPotConnector.2
  N12: R2.Pin_1, C2.0, WheelPotConnector.2
  N13: LevelShifter1.LV2, ToF_VL53L4CD.2
  N14: LevelShifter1.LV1, ToF_VL53L4CD.1

notes:
  STRIX - controller takeover, Variant B (PWM wiper synthesis)
  The Nano synthesizes the two wiper voltages that the handheld
  controller's trigger and steering pots used to produce. Each
  channel is a 4.7k + 1uF RC low-pass filter on a Timer1 PWM pin.
  D9 = throttle, D10 = steering, A0 = controller rail sense.
  The Nano is rotated so its USB end faces the left board edge;
  the phone's OTG cable exits left and powers the Nano.
  FORWARD-PERCEPTION ARRAY (above the board)
  HC-SR04 ultrasonics, front-left and front-right corners:
  front-left TRIG/ECHO -> D2 / D3
  front-right TRIG/ECHO -> D4 / D5
  VCC -> top + rail, GND -> top - rail
  Mount them on the corners angled ~15 deg outward at bumper
  height. Left/right is the CAR's perspective, not yours.
  Placement and aiming: docs/sensor-wiring.md
  3.3V TIME-OF-FLIGHT SENSOR - the centre beam
  The 4-pin header stands in for the VL53L4CD / Modulino
  Distance module; Fritzing has no part for it.
  SDA/SCL cross a bidirectional I2C level shifter: the Nano's
  I2C is 5V logic and the module is 3.3V-only and NOT 5V
  tolerant. HV side faces the Nano (A4/A5 + 5V), LV side faces
  the module.
  ORANGE 3V3 runs straight off the Nano's 3V3 pin - never a 5V
  rail - and drives only this module (~50mA budget).
  THE HANDHELD CONTROLLER'S POT SOCKETS
  The two 3-pin connectors are the sockets the mechanical pots
  unplug from. On both, pin 2 (CENTRE) is the WIPER - that is
  what the meter found on this build, where the BLACK harness
  wire was the wiper, not the colour convention's white.
  pin 1 HIGH - controller rail, sensed by A0 (PURPLE)
  pin 2 WIPER - driven by the RC filter (BLUE / GREEN)
  pin 3 LOW - controller ground (BLACK)
  Pins 1 and 3 are commoned inside the controller, so one rail
  wire and one ground wire serve both sockets.
  PURPLE is the rail sense: it scales every PWM duty to the
  sagging AA rail so calibrated neutral cannot drift. Do not
  omit it. Identify the wiper BEFORE cutting anything:
  docs/pot-identification.md
